// Logisim project ProcessadorFinal-somador_plus.circ as structural Verilog: 14 circuits, main circuit Estrutura ULA
module \Célula_ULA  (
  input  [5:0] Selecionador,
  input  Carry_in__vem_1,
  input  Valor_A,
  input  Valor_B,
  input  Less,
  output \Saída ,
  output Set,
  output Carry_out__Vai_1
);

  wire adder_1_cout, adder_1_out, and_1_out, multiplexer_1_out, multiplexer_2_out, or_1_out,
       subtractor_1_bout, xor_1_out;

  and and_1 (and_1_out, Valor_A, Valor_B);
  or or_1 (or_1_out, Valor_A, Valor_B);
  xor xor_1 (xor_1_out, Valor_A, Valor_B);
  Adder #(.width(1)) adder_1 (.a(Valor_A), .b(Valor_B), .out(adder_1_out), .cin(Carry_in__vem_1), .cout(adder_1_cout));
  Subtractor #(.width(1)) subtractor_1 (
    .a(Valor_A), .b(Valor_B), .out(Set), .bin(Carry_in__vem_1), .bout(subtractor_1_bout));
  Multiplexer #(.select(5), .enable("false")) multiplexer_1 (
    .in0(and_1_out), .in1(or_1_out), .in2(xor_1_out), .in3(adder_1_out), .in4(adder_1_out), .in5(Set),
    .in6(Less), .out(multiplexer_1_out), .sel(Selecionador[4:0]));  // open: in7, in8, in9, in10, in11, in12, in13, in14, in15, in16, in17, in18, in19, in20, in21, in22, in23, in24, in25, in26, in27, in28, in29, in30, in31
  Multiplexer #(.select(5), .enable("false")) multiplexer_2 (
    .in0(adder_1_out), .in1(Set), .out(multiplexer_2_out), .sel(Selecionador[4:0]));  // open: in2, in3, in4, in5, in6, in7, in8, in9, in10, in11, in12, in13, in14, in15, in16, in17, in18, in19, in20, in21, in22, in23, in24, in25, in26, in27, in28, in29, in30, in31
  Multiplexer #(.select(5), .enable("false")) multiplexer_3 (
    .in3(adder_1_cout), .in4(adder_1_cout), .in5(subtractor_1_bout), .in6(subtractor_1_bout),
    .out(Carry_out__Vai_1), .sel(Selecionador[4:0]));  // open: in0, in1, in2, in7, in8, in9, in10, in11, in12, in13, in14, in15, in16, in17, in18, in19, in20, in21, in22, in23, in24, in25, in26, in27, in28, in29, in30, in31
  Multiplexer #(.enable("false")) multiplexer_4 (
    .in0(multiplexer_1_out), .in1(multiplexer_2_out), .out(\Saída ), .sel(Selecionador[5]));

  // Notes on the sheet:
  //   000000 - AND
  //   000001 - OR
  //   000010 - XOR
  //   000011 - Somador inteiros
  //   000100 - Somador naturais
  //   000101 - Subtrator de naturais
  //   LEGENDA
  //   00110 - SLT (Se o valor de A < B) COMPARADOR 
endmodule

module Estrutura_ULA (
  input  [31:0] Valor_A,
  input  [5:0] in_2,
  input  [31:0] Valor_B,
  output [31:0] \Saída ,
  output Zero,
  output \Saída_do_overflow 
);

  wire \célula_ula_1_carry_out__vai_1 , \célula_ula_2_carry_out__vai_1 , \célula_ula_3_carry_out__vai_1 ,
       \célula_ula_4_carry_out__vai_1 , \célula_ula_5_carry_out__vai_1 , \célula_ula_6_carry_out__vai_1 ,
       \célula_ula_7_carry_out__vai_1 , \célula_ula_8_carry_out__vai_1 , \célula_ula_9_carry_out__vai_1 ,
       \célula_ula_10_carry_out__vai_1 , \célula_ula_11_carry_out__vai_1 , \célula_ula_12_carry_out__vai_1 ,
       \célula_ula_13_carry_out__vai_1 , \célula_ula_14_carry_out__vai_1 , \célula_ula_15_carry_out__vai_1 ,
       \célula_ula_16_carry_out__vai_1 , \célula_ula_17_carry_out__vai_1 , \célula_ula_18_carry_out__vai_1 ,
       \célula_ula_19_carry_out__vai_1 , \célula_ula_20_carry_out__vai_1 , \célula_ula_21_carry_out__vai_1 ,
       \célula_ula_22_carry_out__vai_1 , \célula_ula_23_carry_out__vai_1 , \célula_ula_24_carry_out__vai_1 ,
       \célula_ula_25_carry_out__vai_1 , \célula_ula_26_carry_out__vai_1 , \célula_ula_27_carry_out__vai_1 ,
       \célula_ula_28_carry_out__vai_1 , \célula_ula_29_carry_out__vai_1 , \célula_ula_30_carry_out__vai_1 ,
       \célula_ula_31_carry_out__vai_1 , \célula_ula_32_set ;
  wire [3:2] \célula_ula_32_carry_out__vai_1 ;
  wire [30:0] \célula_ula_1_saída ;
  wire [31:0] \sll_1_saída , \sra_1_saída , \srl_1_saída ;

  \Célula_ULA  \célula_ula_1  (
    .Valor_A(Valor_A[0]), .Valor_B(Valor_B[0]), .Less(\célula_ula_32_set ),
    .\Saída (\célula_ula_1_saída [0]), .Carry_in__vem_1(1'b0), .Selecionador(in_2),
    .Carry_out__Vai_1(\célula_ula_1_carry_out__vai_1 ));  // open: Set
  \Célula_ULA  \célula_ula_2  (
    .Valor_A(Valor_A[1]), .Valor_B(Valor_B[1]), .Less(1'b0), .\Saída (\célula_ula_1_saída [1]),
    .Carry_in__vem_1(\célula_ula_1_carry_out__vai_1 ), .Selecionador(in_2),
    .Carry_out__Vai_1(\célula_ula_2_carry_out__vai_1 ));  // open: Set
  \Célula_ULA  \célula_ula_3  (
    .Valor_A(Valor_A[2]), .Valor_B(Valor_B[2]), .Less(1'b0), .\Saída (\célula_ula_1_saída [2]),
    .Carry_in__vem_1(\célula_ula_2_carry_out__vai_1 ), .Selecionador(in_2),
    .Carry_out__Vai_1(\célula_ula_3_carry_out__vai_1 ));  // open: Set
  \Célula_ULA  \célula_ula_4  (
    .Valor_A(Valor_A[3]), .Valor_B(Valor_B[3]), .Less(1'b0), .\Saída (\célula_ula_1_saída [3]),
    .Carry_in__vem_1(\célula_ula_3_carry_out__vai_1 ), .Selecionador(in_2),
    .Carry_out__Vai_1(\célula_ula_4_carry_out__vai_1 ));  // open: Set
  \Célula_ULA  \célula_ula_5  (
    .Valor_A(Valor_A[4]), .Valor_B(Valor_B[4]), .Less(1'b0), .\Saída (\célula_ula_1_saída [4]),
    .Carry_in__vem_1(\célula_ula_4_carry_out__vai_1 ), .Selecionador(in_2),
    .Carry_out__Vai_1(\célula_ula_5_carry_out__vai_1 ));  // open: Set
  \Célula_ULA  \célula_ula_6  (
    .Valor_A(Valor_A[5]), .Valor_B(Valor_B[5]), .Less(1'b0), .\Saída (\célula_ula_1_saída [5]),
    .Carry_in__vem_1(\célula_ula_5_carry_out__vai_1 ), .Selecionador(in_2),
    .Carry_out__Vai_1(\célula_ula_6_carry_out__vai_1 ));  // open: Set
  \Célula_ULA  \célula_ula_7  (
    .Valor_A(Valor_A[6]), .Valor_B(Valor_B[6]), .Less(1'b0), .\Saída (\célula_ula_1_saída [6]),
    .Carry_in__vem_1(\célula_ula_6_carry_out__vai_1 ), .Selecionador(in_2),
    .Carry_out__Vai_1(\célula_ula_7_carry_out__vai_1 ));  // open: Set
  \Célula_ULA  \célula_ula_8  (
    .Valor_A(Valor_A[7]), .Valor_B(Valor_B[7]), .Less(1'b0), .\Saída (\célula_ula_1_saída [7]),
    .Carry_in__vem_1(\célula_ula_7_carry_out__vai_1 ), .Selecionador(in_2),
    .Carry_out__Vai_1(\célula_ula_8_carry_out__vai_1 ));  // open: Set
  \Célula_ULA  \célula_ula_9  (
    .Valor_A(Valor_A[8]), .Valor_B(Valor_B[8]), .Less(1'b0), .\Saída (\célula_ula_1_saída [8]),
    .Carry_in__vem_1(\célula_ula_8_carry_out__vai_1 ), .Selecionador(in_2),
    .Carry_out__Vai_1(\célula_ula_9_carry_out__vai_1 ));  // open: Set
  \Célula_ULA  \célula_ula_10  (
    .Valor_A(Valor_A[9]), .Valor_B(Valor_B[9]), .Less(1'b0), .\Saída (\célula_ula_1_saída [9]),
    .Carry_in__vem_1(\célula_ula_9_carry_out__vai_1 ), .Selecionador(in_2),
    .Carry_out__Vai_1(\célula_ula_10_carry_out__vai_1 ));  // open: Set
  \Célula_ULA  \célula_ula_11  (
    .Valor_A(Valor_A[10]), .Valor_B(Valor_B[10]), .Less(1'b0), .\Saída (\célula_ula_1_saída [10]),
    .Carry_in__vem_1(\célula_ula_10_carry_out__vai_1 ), .Selecionador(in_2),
    .Carry_out__Vai_1(\célula_ula_11_carry_out__vai_1 ));  // open: Set
  \Célula_ULA  \célula_ula_12  (
    .Valor_A(Valor_A[11]), .Valor_B(Valor_B[11]), .Less(1'b0), .\Saída (\célula_ula_1_saída [11]),
    .Carry_in__vem_1(\célula_ula_11_carry_out__vai_1 ), .Selecionador(in_2),
    .Carry_out__Vai_1(\célula_ula_12_carry_out__vai_1 ));  // open: Set
  \Célula_ULA  \célula_ula_13  (
    .Valor_A(Valor_A[12]), .Valor_B(Valor_B[12]), .Less(1'b0), .\Saída (\célula_ula_1_saída [12]),
    .Carry_in__vem_1(\célula_ula_12_carry_out__vai_1 ), .Selecionador(in_2),
    .Carry_out__Vai_1(\célula_ula_13_carry_out__vai_1 ));  // open: Set
  \Célula_ULA  \célula_ula_14  (
    .Valor_A(Valor_A[13]), .Valor_B(Valor_B[13]), .Less(1'b0), .\Saída (\célula_ula_1_saída [13]),
    .Carry_in__vem_1(\célula_ula_13_carry_out__vai_1 ), .Selecionador(in_2),
    .Carry_out__Vai_1(\célula_ula_14_carry_out__vai_1 ));  // open: Set
  \Célula_ULA  \célula_ula_15  (
    .Valor_A(Valor_A[14]), .Valor_B(Valor_B[14]), .Less(1'b0), .\Saída (\célula_ula_1_saída [14]),
    .Carry_in__vem_1(\célula_ula_14_carry_out__vai_1 ), .Selecionador(in_2),
    .Carry_out__Vai_1(\célula_ula_15_carry_out__vai_1 ));  // open: Set
  \Célula_ULA  \célula_ula_16  (
    .Valor_A(Valor_A[15]), .Valor_B(Valor_B[15]), .Less(1'b0), .\Saída (\célula_ula_1_saída [15]),
    .Carry_in__vem_1(\célula_ula_15_carry_out__vai_1 ), .Selecionador(in_2),
    .Carry_out__Vai_1(\célula_ula_16_carry_out__vai_1 ));  // open: Set
  \Célula_ULA  \célula_ula_17  (
    .Valor_A(Valor_A[16]), .Valor_B(Valor_B[16]), .Less(1'b0), .\Saída (\célula_ula_1_saída [16]),
    .Carry_in__vem_1(\célula_ula_16_carry_out__vai_1 ), .Selecionador(in_2),
    .Carry_out__Vai_1(\célula_ula_17_carry_out__vai_1 ));  // open: Set
  \Célula_ULA  \célula_ula_18  (
    .Valor_A(Valor_A[17]), .Valor_B(Valor_B[17]), .Less(1'b0), .\Saída (\célula_ula_1_saída [17]),
    .Carry_in__vem_1(\célula_ula_17_carry_out__vai_1 ), .Selecionador(in_2),
    .Carry_out__Vai_1(\célula_ula_18_carry_out__vai_1 ));  // open: Set
  \Célula_ULA  \célula_ula_19  (
    .Valor_A(Valor_A[18]), .Valor_B(Valor_B[18]), .Less(1'b0), .\Saída (\célula_ula_1_saída [18]),
    .Carry_in__vem_1(\célula_ula_18_carry_out__vai_1 ), .Selecionador(in_2),
    .Carry_out__Vai_1(\célula_ula_19_carry_out__vai_1 ));  // open: Set
  \Célula_ULA  \célula_ula_20  (
    .Valor_A(Valor_A[19]), .Valor_B(Valor_B[19]), .Less(1'b0), .\Saída (\célula_ula_1_saída [19]),
    .Carry_in__vem_1(\célula_ula_19_carry_out__vai_1 ), .Selecionador(in_2),
    .Carry_out__Vai_1(\célula_ula_20_carry_out__vai_1 ));  // open: Set
  \Célula_ULA  \célula_ula_21  (
    .Valor_A(Valor_A[20]), .Valor_B(Valor_B[20]), .Less(1'b0), .\Saída (\célula_ula_1_saída [20]),
    .Carry_in__vem_1(\célula_ula_20_carry_out__vai_1 ), .Selecionador(in_2),
    .Carry_out__Vai_1(\célula_ula_21_carry_out__vai_1 ));  // open: Set
  \Célula_ULA  \célula_ula_22  (
    .Valor_A(Valor_A[21]), .Valor_B(Valor_B[21]), .Less(1'b0), .\Saída (\célula_ula_1_saída [21]),
    .Carry_in__vem_1(\célula_ula_21_carry_out__vai_1 ), .Selecionador(in_2),
    .Carry_out__Vai_1(\célula_ula_22_carry_out__vai_1 ));  // open: Set
  \Célula_ULA  \célula_ula_23  (
    .Valor_A(Valor_A[22]), .Valor_B(Valor_B[22]), .Less(1'b0), .\Saída (\célula_ula_1_saída [22]),
    .Carry_in__vem_1(\célula_ula_22_carry_out__vai_1 ), .Selecionador(in_2),
    .Carry_out__Vai_1(\célula_ula_23_carry_out__vai_1 ));  // open: Set
  \Célula_ULA  \célula_ula_24  (
    .Valor_A(Valor_A[23]), .Valor_B(Valor_B[23]), .Less(1'b0), .\Saída (\célula_ula_1_saída [23]),
    .Carry_in__vem_1(\célula_ula_23_carry_out__vai_1 ), .Selecionador(in_2),
    .Carry_out__Vai_1(\célula_ula_24_carry_out__vai_1 ));  // open: Set
  \Célula_ULA  \célula_ula_25  (
    .Valor_A(Valor_A[24]), .Valor_B(Valor_B[24]), .Less(1'b0), .\Saída (\célula_ula_1_saída [24]),
    .Carry_in__vem_1(\célula_ula_24_carry_out__vai_1 ), .Selecionador(in_2),
    .Carry_out__Vai_1(\célula_ula_25_carry_out__vai_1 ));  // open: Set
  \Célula_ULA  \célula_ula_26  (
    .Valor_A(Valor_A[25]), .Valor_B(Valor_B[25]), .Less(1'b0), .\Saída (\célula_ula_1_saída [25]),
    .Carry_in__vem_1(\célula_ula_25_carry_out__vai_1 ), .Selecionador(in_2),
    .Carry_out__Vai_1(\célula_ula_26_carry_out__vai_1 ));  // open: Set
  \Célula_ULA  \célula_ula_27  (
    .Valor_A(Valor_A[26]), .Valor_B(Valor_B[26]), .Less(1'b0), .\Saída (\célula_ula_1_saída [26]),
    .Carry_in__vem_1(\célula_ula_26_carry_out__vai_1 ), .Selecionador(in_2),
    .Carry_out__Vai_1(\célula_ula_27_carry_out__vai_1 ));  // open: Set
  \Célula_ULA  \célula_ula_28  (
    .Valor_A(Valor_A[27]), .Valor_B(Valor_B[27]), .Less(1'b0), .\Saída (\célula_ula_1_saída [27]),
    .Carry_in__vem_1(\célula_ula_27_carry_out__vai_1 ), .Selecionador(in_2),
    .Carry_out__Vai_1(\célula_ula_28_carry_out__vai_1 ));  // open: Set
  \Célula_ULA  \célula_ula_29  (
    .Valor_A(Valor_A[28]), .Valor_B(Valor_B[28]), .Less(1'b0), .\Saída (\célula_ula_1_saída [28]),
    .Carry_in__vem_1(\célula_ula_28_carry_out__vai_1 ), .Selecionador(in_2),
    .Carry_out__Vai_1(\célula_ula_29_carry_out__vai_1 ));  // open: Set
  \Célula_ULA  \célula_ula_30  (
    .Valor_A(Valor_A[29]), .Valor_B(Valor_B[29]), .Less(1'b0), .\Saída (\célula_ula_1_saída [29]),
    .Carry_in__vem_1(\célula_ula_29_carry_out__vai_1 ), .Selecionador(in_2),
    .Carry_out__Vai_1(\célula_ula_30_carry_out__vai_1 ));  // open: Set
  \Célula_ULA  \célula_ula_31  (
    .Valor_A(Valor_A[30]), .Valor_B(Valor_B[30]), .Less(1'b0), .\Saída (\célula_ula_1_saída [30]),
    .Carry_in__vem_1(\célula_ula_30_carry_out__vai_1 ), .Selecionador(in_2),
    .Carry_out__Vai_1(\célula_ula_31_carry_out__vai_1 ));  // open: Set
  \Célula_ULA  \célula_ula_32  (
    .Valor_A(Valor_A[31]), .Valor_B(Valor_B[31]), .Less(1'b0), .\Saída (\célula_ula_32_carry_out__vai_1 [2]),
    .Carry_in__vem_1(\célula_ula_31_carry_out__vai_1 ), .Selecionador(in_2), .Set(\célula_ula_32_set ),
    .Carry_out__Vai_1(\célula_ula_32_carry_out__vai_1 [3]));
  Overflow overflow_1 (
    .Entrada_dos_valores({\célula_ula_32_carry_out__vai_1 , Valor_B[31], Valor_A[31]}),
    .\Saída_do_overflow (\Saída_do_overflow ), .in_1(in_2));
  SLL sll_1 (.ENTRADA(Valor_A), .\SAÍDA (\sll_1_saída ));
  SRL srl_1 (.ENTRADA(Valor_A), .\SAÍDA (\srl_1_saída ));
  SRA sra_1 (.ENTRADA(Valor_A), .\SAÍDA (\sra_1_saída ));
  Multiplexer #(.select(5), .width(32), .enable("false")) multiplexer_1 (
    .in7(\sll_1_saída ), .in8(\srl_1_saída ), .in9(\sra_1_saída ),
    .out({\célula_ula_32_carry_out__vai_1 [2], \célula_ula_1_saída }), .sel(in_2[4:0]));  // open: in0, in1, in2, in3, in4, in5, in6, in10, in11, in12, in13, in14, in15, in16, in17, in18, in19, in20, in21, in22, in23, in24, in25, in26, in27, in28, in29, in30, in31
  nor nor_1 (Zero, \célula_ula_1_saída [0], \célula_ula_1_saída [1], \célula_ula_1_saída [2], \célula_ula_1_saída [3], \célula_ula_1_saída [4], \célula_ula_1_saída [5], \célula_ula_1_saída [6], \célula_ula_1_saída [7], \célula_ula_1_saída [8], \célula_ula_1_saída [9], \célula_ula_1_saída [10], \célula_ula_1_saída [11], \célula_ula_1_saída [12], \célula_ula_1_saída [13], \célula_ula_1_saída [14], \célula_ula_1_saída [15], \célula_ula_1_saída [16], \célula_ula_1_saída [17], \célula_ula_1_saída [18], \célula_ula_1_saída [19], \célula_ula_1_saída [20], \célula_ula_1_saída [21], \célula_ula_1_saída [22], \célula_ula_1_saída [23], \célula_ula_1_saída [24], \célula_ula_1_saída [25], \célula_ula_1_saída [26], \célula_ula_1_saída [27], \célula_ula_1_saída [28], \célula_ula_1_saída [29], \célula_ula_1_saída [30], \célula_ula_32_carry_out__vai_1 [2]);
  Multiplexer #(.width(32), .enable("false")) multiplexer_2 (
    .in0({\célula_ula_32_carry_out__vai_1 [2], \célula_ula_1_saída }),
    .in1({\célula_ula_32_carry_out__vai_1 [2], \célula_ula_1_saída }), .out(\Saída ), .sel(in_2[5]));

  // Notes on the sheet:
  //   Constante zero
  //   Aterramento
  //   Operador (seleciona a operação)
  //   000000 - AND
  //   000001 - OR
  //   000010 - XOR
  //   000011 - Somador inteiros
  //   000100 - Somador naturais
  //   000101 - Subtrator de naturais
  //   000111 - SLL Desloca o bit para esquerda 
  //   001000 - SRL Desloca o bit para direita 
  //   000110 - SLT (Se o valor de A < B) COMPARADOR 
  //   LEGENDA
  //   001001 - SRA Pega o bit de menor valor e duplica deslocando para a direita
endmodule

module SLL (
  input  [31:0] ENTRADA,
  output [31:0] \SAÍDA 
);


  assign \SAÍDA  = {ENTRADA[30:0], 1'b0};
  // also tied to GND on the sheet: ENTRADA[31]

  // Notes on the sheet:
  //   SLL
  //   Desloca o bit para esquerda
endmodule

module SRL (
  input  [31:0] ENTRADA,
  output [31:0] \SAÍDA 
);


  assign \SAÍDA  = {1'b0, ENTRADA[31:1]};
  // also tied to GND on the sheet: ENTRADA[0]

  // Notes on the sheet:
  //   SRL
  //   Desloca o bit para direita
endmodule

module SRA (
  input  [31:0] ENTRADA,
  output [31:0] \SAÍDA 
);


  assign \SAÍDA  = {{2{ENTRADA[31]}}, ENTRADA[30:1]};
  // also tied to GND on the sheet: ENTRADA[0]

  // Notes on the sheet:
  //   SRA
  //   Deslocador aritmético: pega o bit menos significativo, cópia e desloca para direita
endmodule

module Overflow (
  input  [5:0] in_1,
  input  [3:0] Entrada_dos_valores,
  output \Saída_do_overflow 
);

  wire and_1_out, and_2_out, and_3_out, and_4_out, multiplexer_1_out, or_1_out, or_2_out;

  and and_1 (and_1_out, Entrada_dos_valores[0], Entrada_dos_valores[1], ~Entrada_dos_valores[2]);  // AND_Gate
  and and_2 (and_2_out, ~Entrada_dos_valores[0], ~Entrada_dos_valores[1], Entrada_dos_valores[2]);  // AND_Gate
  and and_3 (and_3_out, ~Entrada_dos_valores[0], Entrada_dos_valores[1], Entrada_dos_valores[2]);  // AND_Gate
  and and_4 (and_4_out, Entrada_dos_valores[0], ~Entrada_dos_valores[1], ~Entrada_dos_valores[2]);  // AND_Gate
  or or_1 (or_1_out, and_1_out, and_2_out);
  or or_2 (or_2_out, and_3_out, and_4_out);
  Multiplexer #(.select(5), .enable("false")) multiplexer_1 (
    .in3(or_1_out), .in4(Entrada_dos_valores[3]), .in5(or_2_out), .out(multiplexer_1_out), .sel(in_1[4:0]));  // open: in0, in1, in2, in6, in7, in8, in9, in10, in11, in12, in13, in14, in15, in16, in17, in18, in19, in20, in21, in22, in23, in24, in25, in26, in27, in28, in29, in30, in31
  Multiplexer #(.enable("false")) multiplexer_2 (
    .in0(multiplexer_1_out), .in1(multiplexer_1_out), .out(\Saída_do_overflow ), .sel(in_1[5]));

  // Notes on the sheet:
  //   Operador (seleciona a operação)
endmodule

module ULA (
  input  [5:0] Operador,
  input  [31:0] in_2,
  input  [31:0] in_3,
  output [31:0] out_4,
  output Zero
);

  wire \estrutura_ula_1_saída_do_overflow ;

  Estrutura_ULA estrutura_ula_1 (
    .Valor_A(in_2), .Valor_B(in_3), .in_2(Operador), .\Saída (out_4), .Zero(Zero),
    .\Saída_do_overflow (\estrutura_ula_1_saída_do_overflow ));
  LED led_1 (.in(\estrutura_ula_1_saída_do_overflow ));

  // Notes on the sheet:
  //   A
  //   B
  //   Overflow
  //   Saída
  //   000000 - AND
  //   000001 - OR
  //   000010 - XOR
  //   000011 - Somador inteiros
  //   000100 - Somador naturais
  //   000101 - Subtrator de naturais
  //   000110 - SLT (Se o valor de A < B) COMPARADOR 
  //   000111 - SLL Desloca o bit para esquerda 
  //   001000 - SRL Desloca o bit para direita 
  //   LEGENDA
  //   001001 - SRA Pega o bit de menor valor e duplica deslocando para a direita
endmodule

module Registrador (
  input  Reset,
  input  [31:0] Dados_de_entrada,
  input  Clock,
  output [31:0] \Dados_de_saída 
);

  D_Flip_Flop d_ff_1 (
    .clk(Clock), .D(Dados_de_entrada[0]), .Q(\Dados_de_saída [0]), .reset(Reset));  // open: Qn, preset, en
  D_Flip_Flop d_ff_2 (
    .clk(Clock), .D(Dados_de_entrada[16]), .Q(\Dados_de_saída [16]), .reset(Reset));  // open: Qn, preset, en
  D_Flip_Flop d_ff_3 (
    .clk(Clock), .D(Dados_de_entrada[1]), .Q(\Dados_de_saída [1]), .reset(Reset));  // open: Qn, preset, en
  D_Flip_Flop d_ff_4 (
    .clk(Clock), .D(Dados_de_entrada[17]), .Q(\Dados_de_saída [17]), .reset(Reset));  // open: Qn, preset, en
  D_Flip_Flop d_ff_5 (
    .clk(Clock), .D(Dados_de_entrada[2]), .Q(\Dados_de_saída [2]), .reset(Reset));  // open: Qn, preset, en
  D_Flip_Flop d_ff_6 (
    .clk(Clock), .D(Dados_de_entrada[18]), .Q(\Dados_de_saída [18]), .reset(Reset));  // open: Qn, preset, en
  D_Flip_Flop d_ff_7 (
    .clk(Clock), .D(Dados_de_entrada[3]), .Q(\Dados_de_saída [3]), .reset(Reset));  // open: Qn, preset, en
  D_Flip_Flop d_ff_8 (
    .clk(Clock), .D(Dados_de_entrada[19]), .Q(\Dados_de_saída [19]), .reset(Reset));  // open: Qn, preset, en
  D_Flip_Flop d_ff_9 (
    .clk(Clock), .D(Dados_de_entrada[4]), .Q(\Dados_de_saída [4]), .reset(Reset));  // open: Qn, preset, en
  D_Flip_Flop d_ff_10 (
    .clk(Clock), .D(Dados_de_entrada[20]), .Q(\Dados_de_saída [20]), .reset(Reset));  // open: Qn, preset, en
  D_Flip_Flop d_ff_11 (
    .clk(Clock), .D(Dados_de_entrada[5]), .Q(\Dados_de_saída [5]), .reset(Reset));  // open: Qn, preset, en
  D_Flip_Flop d_ff_12 (
    .clk(Clock), .D(Dados_de_entrada[21]), .Q(\Dados_de_saída [21]), .reset(Reset));  // open: Qn, preset, en
  D_Flip_Flop d_ff_13 (
    .clk(Clock), .D(Dados_de_entrada[6]), .Q(\Dados_de_saída [6]), .reset(Reset));  // open: Qn, preset, en
  D_Flip_Flop d_ff_14 (
    .clk(Clock), .D(Dados_de_entrada[22]), .Q(\Dados_de_saída [22]), .reset(Reset));  // open: Qn, preset, en
  D_Flip_Flop d_ff_15 (
    .clk(Clock), .D(Dados_de_entrada[7]), .Q(\Dados_de_saída [7]), .reset(Reset));  // open: Qn, preset, en
  D_Flip_Flop d_ff_16 (
    .clk(Clock), .D(Dados_de_entrada[23]), .Q(\Dados_de_saída [23]), .reset(Reset));  // open: Qn, preset, en
  D_Flip_Flop d_ff_17 (
    .clk(Clock), .D(Dados_de_entrada[8]), .Q(\Dados_de_saída [8]), .reset(Reset));  // open: Qn, preset, en
  D_Flip_Flop d_ff_18 (
    .clk(Clock), .D(Dados_de_entrada[24]), .Q(\Dados_de_saída [24]), .reset(Reset));  // open: Qn, preset, en
  D_Flip_Flop d_ff_19 (
    .clk(Clock), .D(Dados_de_entrada[9]), .Q(\Dados_de_saída [9]), .reset(Reset));  // open: Qn, preset, en
  D_Flip_Flop d_ff_20 (
    .clk(Clock), .D(Dados_de_entrada[25]), .Q(\Dados_de_saída [25]), .reset(Reset));  // open: Qn, preset, en
  D_Flip_Flop d_ff_21 (
    .clk(Clock), .D(Dados_de_entrada[10]), .Q(\Dados_de_saída [10]), .reset(Reset));  // open: Qn, preset, en
  D_Flip_Flop d_ff_22 (
    .clk(Clock), .D(Dados_de_entrada[26]), .Q(\Dados_de_saída [26]), .reset(Reset));  // open: Qn, preset, en
  D_Flip_Flop d_ff_23 (
    .clk(Clock), .D(Dados_de_entrada[11]), .Q(\Dados_de_saída [11]), .reset(Reset));  // open: Qn, preset, en
  D_Flip_Flop d_ff_24 (
    .clk(Clock), .D(Dados_de_entrada[27]), .Q(\Dados_de_saída [27]), .reset(Reset));  // open: Qn, preset, en
  D_Flip_Flop d_ff_25 (
    .clk(Clock), .D(Dados_de_entrada[12]), .Q(\Dados_de_saída [12]), .reset(Reset));  // open: Qn, preset, en
  D_Flip_Flop d_ff_26 (
    .clk(Clock), .D(Dados_de_entrada[28]), .Q(\Dados_de_saída [28]), .reset(Reset));  // open: Qn, preset, en
  D_Flip_Flop d_ff_27 (
    .clk(Clock), .D(Dados_de_entrada[13]), .Q(\Dados_de_saída [13]), .reset(Reset));  // open: Qn, preset, en
  D_Flip_Flop d_ff_28 (
    .clk(Clock), .D(Dados_de_entrada[29]), .Q(\Dados_de_saída [29]), .reset(Reset));  // open: Qn, preset, en
  D_Flip_Flop d_ff_29 (
    .clk(Clock), .D(Dados_de_entrada[14]), .Q(\Dados_de_saída [14]), .reset(Reset));  // open: Qn, preset, en
  D_Flip_Flop d_ff_30 (
    .clk(Clock), .D(Dados_de_entrada[30]), .Q(\Dados_de_saída [30]), .reset(Reset));  // open: Qn, preset, en
  D_Flip_Flop d_ff_31 (
    .clk(Clock), .D(Dados_de_entrada[15]), .Q(\Dados_de_saída [15]), .reset(Reset));  // open: Qn, preset, en
  D_Flip_Flop d_ff_32 (
    .clk(Clock), .D(Dados_de_entrada[31]), .Q(\Dados_de_saída [31]), .reset(Reset));  // open: Qn, preset, en
endmodule

module Banco_Registradores (
  input  [31:0] Entrada,
  input  Reset,
  input  [4:0] Op_1,
  input  [4:0] Op_2,
  input  Clock,
  input  [4:0] Op_C,
  output [31:0] \Saída_A ,
  output [31:0] \Saída_B 
);

  wire demultiplexer_1_out0, demultiplexer_1_out1, demultiplexer_1_out2, demultiplexer_1_out3,
       demultiplexer_1_out4, demultiplexer_1_out5, demultiplexer_1_out6, demultiplexer_1_out7,
       demultiplexer_1_out8, demultiplexer_1_out9, demultiplexer_1_out10, demultiplexer_1_out11,
       demultiplexer_1_out12, demultiplexer_1_out13, demultiplexer_1_out14, demultiplexer_1_out15,
       demultiplexer_1_out16, demultiplexer_1_out17, demultiplexer_1_out18, demultiplexer_1_out19,
       demultiplexer_1_out20, demultiplexer_1_out21, demultiplexer_1_out22, demultiplexer_1_out23,
       demultiplexer_1_out24, demultiplexer_1_out25, demultiplexer_1_out26, demultiplexer_1_out27,
       demultiplexer_1_out28, demultiplexer_1_out29, demultiplexer_1_out30, demultiplexer_1_out31;
  wire [31:0] \registrador_1_dados_de_saída , \registrador_2_dados_de_saída , \registrador_3_dados_de_saída ,
       \registrador_4_dados_de_saída , \registrador_5_dados_de_saída , \registrador_6_dados_de_saída ,
       \registrador_7_dados_de_saída , \registrador_8_dados_de_saída , \registrador_9_dados_de_saída ,
       \registrador_10_dados_de_saída , \registrador_11_dados_de_saída , \registrador_12_dados_de_saída ,
       \registrador_13_dados_de_saída , \registrador_14_dados_de_saída , \registrador_15_dados_de_saída ,
       \registrador_16_dados_de_saída , \registrador_17_dados_de_saída , \registrador_18_dados_de_saída ,
       \registrador_19_dados_de_saída , \registrador_20_dados_de_saída , \registrador_21_dados_de_saída ,
       \registrador_22_dados_de_saída , \registrador_23_dados_de_saída , \registrador_24_dados_de_saída ,
       \registrador_25_dados_de_saída , \registrador_26_dados_de_saída , \registrador_27_dados_de_saída ,
       \registrador_28_dados_de_saída , \registrador_29_dados_de_saída , \registrador_30_dados_de_saída ,
       \registrador_31_dados_de_saída , undriven;

  Demultiplexer #(.select(5), .enable("false")) demultiplexer_1 (
    .out0(demultiplexer_1_out0), .out1(demultiplexer_1_out1), .out2(demultiplexer_1_out2),
    .out3(demultiplexer_1_out3), .out4(demultiplexer_1_out4), .out5(demultiplexer_1_out5),
    .out6(demultiplexer_1_out6), .out7(demultiplexer_1_out7), .out8(demultiplexer_1_out8),
    .out9(demultiplexer_1_out9), .out10(demultiplexer_1_out10), .out11(demultiplexer_1_out11),
    .out12(demultiplexer_1_out12), .out13(demultiplexer_1_out13), .out14(demultiplexer_1_out14),
    .out15(demultiplexer_1_out15), .out16(demultiplexer_1_out16), .out17(demultiplexer_1_out17),
    .out18(demultiplexer_1_out18), .out19(demultiplexer_1_out19), .out20(demultiplexer_1_out20),
    .out21(demultiplexer_1_out21), .out22(demultiplexer_1_out22), .out23(demultiplexer_1_out23),
    .out24(demultiplexer_1_out24), .out25(demultiplexer_1_out25), .out26(demultiplexer_1_out26),
    .out27(demultiplexer_1_out27), .out28(demultiplexer_1_out28), .out29(demultiplexer_1_out29),
    .out30(demultiplexer_1_out30), .out31(demultiplexer_1_out31), .in(Clock), .sel(Op_C));
  Registrador registrador_1 (
    .Clock(demultiplexer_1_out0), .\Dados_de_saída (\registrador_1_dados_de_saída ),
    .Dados_de_entrada(Entrada), .Reset(Reset));
  Registrador registrador_2 (
    .Clock(demultiplexer_1_out1), .\Dados_de_saída (\registrador_2_dados_de_saída ),
    .Dados_de_entrada(Entrada), .Reset(Reset));
  Registrador registrador_3 (
    .Clock(demultiplexer_1_out2), .\Dados_de_saída (\registrador_3_dados_de_saída ),
    .Dados_de_entrada(Entrada), .Reset(Reset));
  Registrador registrador_4 (
    .Clock(demultiplexer_1_out3), .\Dados_de_saída (\registrador_4_dados_de_saída ),
    .Dados_de_entrada(Entrada), .Reset(Reset));
  Registrador registrador_5 (
    .Clock(demultiplexer_1_out4), .\Dados_de_saída (\registrador_5_dados_de_saída ),
    .Dados_de_entrada(Entrada), .Reset(Reset));
  Registrador registrador_6 (
    .Clock(demultiplexer_1_out5), .\Dados_de_saída (\registrador_6_dados_de_saída ),
    .Dados_de_entrada(Entrada), .Reset(Reset));
  Registrador registrador_7 (
    .Clock(demultiplexer_1_out6), .\Dados_de_saída (\registrador_7_dados_de_saída ),
    .Dados_de_entrada(Entrada), .Reset(Reset));
  Registrador registrador_8 (
    .Clock(demultiplexer_1_out7), .\Dados_de_saída (\registrador_8_dados_de_saída ),
    .Dados_de_entrada(Entrada), .Reset(Reset));
  Registrador registrador_9 (
    .Clock(demultiplexer_1_out8), .\Dados_de_saída (\registrador_9_dados_de_saída ),
    .Dados_de_entrada(Entrada), .Reset(Reset));
  Registrador registrador_10 (
    .Clock(demultiplexer_1_out9), .\Dados_de_saída (\registrador_10_dados_de_saída ),
    .Dados_de_entrada(Entrada), .Reset(Reset));
  Registrador registrador_11 (
    .Clock(demultiplexer_1_out10), .\Dados_de_saída (\registrador_11_dados_de_saída ),
    .Dados_de_entrada(Entrada), .Reset(Reset));
  Registrador registrador_12 (
    .Clock(demultiplexer_1_out11), .\Dados_de_saída (\registrador_12_dados_de_saída ),
    .Dados_de_entrada(Entrada), .Reset(Reset));
  Registrador registrador_13 (
    .Clock(demultiplexer_1_out12), .\Dados_de_saída (\registrador_13_dados_de_saída ),
    .Dados_de_entrada(Entrada), .Reset(Reset));
  Registrador registrador_14 (
    .Clock(demultiplexer_1_out13), .\Dados_de_saída (\registrador_14_dados_de_saída ),
    .Dados_de_entrada(Entrada), .Reset(Reset));
  Registrador registrador_15 (
    .Clock(demultiplexer_1_out14), .\Dados_de_saída (\registrador_15_dados_de_saída ),
    .Dados_de_entrada(Entrada), .Reset(Reset));
  Registrador registrador_16 (
    .Clock(demultiplexer_1_out15), .\Dados_de_saída (\registrador_16_dados_de_saída ),
    .Dados_de_entrada(Entrada), .Reset(Reset));
  Registrador registrador_17 (
    .Clock(demultiplexer_1_out16), .\Dados_de_saída (\registrador_17_dados_de_saída ),
    .Dados_de_entrada(Entrada), .Reset(Reset));
  Registrador registrador_18 (
    .Clock(demultiplexer_1_out17), .\Dados_de_saída (\registrador_18_dados_de_saída ),
    .Dados_de_entrada(Entrada), .Reset(Reset));
  Registrador registrador_19 (
    .Clock(demultiplexer_1_out18), .\Dados_de_saída (\registrador_19_dados_de_saída ),
    .Dados_de_entrada(Entrada), .Reset(Reset));
  Registrador registrador_20 (
    .Clock(demultiplexer_1_out19), .\Dados_de_saída (\registrador_20_dados_de_saída ),
    .Dados_de_entrada(Entrada), .Reset(Reset));
  Registrador registrador_21 (
    .Clock(demultiplexer_1_out20), .\Dados_de_saída (\registrador_21_dados_de_saída ),
    .Dados_de_entrada(Entrada), .Reset(Reset));
  Registrador registrador_22 (
    .Clock(demultiplexer_1_out21), .\Dados_de_saída (\registrador_22_dados_de_saída ),
    .Dados_de_entrada(Entrada), .Reset(Reset));
  Registrador registrador_23 (
    .Clock(demultiplexer_1_out22), .\Dados_de_saída (\registrador_23_dados_de_saída ),
    .Dados_de_entrada(Entrada), .Reset(Reset));
  Registrador registrador_24 (
    .Clock(demultiplexer_1_out23), .\Dados_de_saída (\registrador_24_dados_de_saída ),
    .Dados_de_entrada(Entrada), .Reset(Reset));
  Registrador registrador_25 (
    .Clock(demultiplexer_1_out24), .\Dados_de_saída (\registrador_25_dados_de_saída ),
    .Dados_de_entrada(Entrada), .Reset(Reset));
  Registrador registrador_26 (
    .Clock(demultiplexer_1_out25), .\Dados_de_saída (\registrador_26_dados_de_saída ),
    .Dados_de_entrada(Entrada), .Reset(Reset));
  Registrador registrador_27 (
    .Clock(demultiplexer_1_out26), .\Dados_de_saída (\registrador_27_dados_de_saída ),
    .Dados_de_entrada(Entrada), .Reset(Reset));
  Registrador registrador_28 (
    .Clock(demultiplexer_1_out27), .\Dados_de_saída (\registrador_28_dados_de_saída ),
    .Dados_de_entrada(Entrada), .Reset(Reset));
  Registrador registrador_29 (
    .Clock(demultiplexer_1_out28), .\Dados_de_saída (\registrador_29_dados_de_saída ),
    .Dados_de_entrada(Entrada), .Reset(Reset));
  Registrador registrador_30 (
    .Clock(demultiplexer_1_out29), .\Dados_de_saída (\registrador_30_dados_de_saída ),
    .Dados_de_entrada(Entrada), .Reset(Reset));
  Registrador registrador_31 (
    .Clock(demultiplexer_1_out30), .\Dados_de_saída (\registrador_31_dados_de_saída ),
    .Dados_de_entrada(Entrada), .Reset(Reset));
  Registrador registrador_32 (
    .Clock(demultiplexer_1_out31), .Dados_de_entrada(Entrada), .Reset(Reset));  // open: Dados_de_saída
  Multiplexer #(.select(5), .width(32), .enable("false")) multiplexer_1 (
    .in0(\registrador_1_dados_de_saída ), .in1(\registrador_2_dados_de_saída ),
    .in2(\registrador_3_dados_de_saída ), .in3(\registrador_4_dados_de_saída ),
    .in4(\registrador_5_dados_de_saída ), .in5(\registrador_6_dados_de_saída ),
    .in6(\registrador_7_dados_de_saída ), .in7(\registrador_8_dados_de_saída ),
    .in8(\registrador_9_dados_de_saída ), .in9(\registrador_10_dados_de_saída ),
    .in10(\registrador_11_dados_de_saída ), .in11(\registrador_12_dados_de_saída ),
    .in12(\registrador_13_dados_de_saída ), .in13(\registrador_14_dados_de_saída ),
    .in14(\registrador_15_dados_de_saída ), .in15(\registrador_16_dados_de_saída ),
    .in16(\registrador_17_dados_de_saída ), .in17(\registrador_18_dados_de_saída ),
    .in18(\registrador_19_dados_de_saída ), .in19(\registrador_20_dados_de_saída ),
    .in20(\registrador_21_dados_de_saída ), .in21(\registrador_22_dados_de_saída ),
    .in22(\registrador_23_dados_de_saída ), .in23(\registrador_24_dados_de_saída ),
    .in24(\registrador_25_dados_de_saída ), .in25(\registrador_26_dados_de_saída ),
    .in26(\registrador_27_dados_de_saída ), .in27(\registrador_28_dados_de_saída ),
    .in28(\registrador_29_dados_de_saída ), .in29(\registrador_30_dados_de_saída ),
    .in30(\registrador_31_dados_de_saída ), .in31(undriven), .out(\Saída_A ), .sel(Op_1));
  Multiplexer #(.select(5), .width(32), .enable("false")) multiplexer_2 (
    .in0(\registrador_1_dados_de_saída ), .in1(\registrador_2_dados_de_saída ),
    .in2(\registrador_3_dados_de_saída ), .in3(\registrador_4_dados_de_saída ),
    .in4(\registrador_5_dados_de_saída ), .in5(\registrador_6_dados_de_saída ),
    .in6(\registrador_7_dados_de_saída ), .in7(\registrador_8_dados_de_saída ),
    .in8(\registrador_9_dados_de_saída ), .in9(\registrador_10_dados_de_saída ),
    .in10(\registrador_11_dados_de_saída ), .in11(\registrador_12_dados_de_saída ),
    .in12(\registrador_13_dados_de_saída ), .in13(\registrador_14_dados_de_saída ),
    .in14(\registrador_15_dados_de_saída ), .in15(\registrador_16_dados_de_saída ),
    .in16(\registrador_17_dados_de_saída ), .in17(\registrador_18_dados_de_saída ),
    .in18(\registrador_19_dados_de_saída ), .in19(\registrador_20_dados_de_saída ),
    .in20(\registrador_21_dados_de_saída ), .in21(\registrador_22_dados_de_saída ),
    .in22(\registrador_23_dados_de_saída ), .in23(\registrador_24_dados_de_saída ),
    .in24(\registrador_25_dados_de_saída ), .in25(\registrador_26_dados_de_saída ),
    .in26(\registrador_27_dados_de_saída ), .in27(\registrador_28_dados_de_saída ),
    .in28(\registrador_29_dados_de_saída ), .in29(\registrador_30_dados_de_saída ),
    .in30(\registrador_31_dados_de_saída ), .in31(undriven), .out(\Saída_B ), .sel(Op_2));
endmodule

module PC (
  input  [7:0] in_1,
  input  Clock,
  input  Reset,
  output [7:0] \Saída 
);

  wire [7:0] adder_1_out;

  Register Registrador (.D(adder_1_out), .Q(\Saída ), .clk(Clock), .clr(Reset));  // open: en
  Adder adder_1 (.a(in_1), .b(\Saída ), .out(adder_1_out));  // open: cin, cout

  // Notes on the sheet:
  //   Entrada do PC
endmodule

module Micro_Processador (
  input  [31:0] Entrada_do_IR,
  input  Reset,
  input  Clock,
  output [7:0] \Saída_do_PC ,
  output Overflow
);

  wire and_1_out, and_2_out, and_3_out, estrutura_ula_1_zero;
  wire [7:0] multiplexer_1_out;
  wire [31:0] \banco_registradores_1_saída_a , \banco_registradores_1_saída_b , \estrutura_ula_1_saída ,
       IR_q, multiplexer_2_out;

  Multiplexer #(.width(8), .enable("false")) multiplexer_1 (
    .in0(8'h1), .in1(IR_q[7:0]), .out(multiplexer_1_out), .sel(and_1_out));
  PC pc_1 (.\Saída (\Saída_do_PC ), .Clock(Clock), .Reset(Reset), .in_1(multiplexer_1_out));
  Register #(.width(32)) IR (.D(Entrada_do_IR), .Q(IR_q), .clk(Clock), .clr(Reset));  // open: en
  Banco_Registradores banco_registradores_1 (
    .Clock(Clock), .\Saída_A (\banco_registradores_1_saída_a ), .\Saída_B (\banco_registradores_1_saída_b ),
    .Reset(Reset), .Entrada(\estrutura_ula_1_saída ), .Op_C(IR_q[15:11]), .Op_1(IR_q[25:21]),
    .Op_2(IR_q[20:16]));
  Multiplexer #(.width(32), .enable("false")) multiplexer_2 (
    .in0(\banco_registradores_1_saída_b ), .in1({{22{IR_q[10]}}, IR_q[9:0]}), .out(multiplexer_2_out),
    .sel(and_3_out));
  and and_1 (and_1_out, estrutura_ula_1_zero, and_2_out);
  Estrutura_ULA estrutura_ula_1 (
    .Valor_A(\banco_registradores_1_saída_a ), .Valor_B(multiplexer_2_out), .in_2(IR_q[31:26]),
    .\Saída (\estrutura_ula_1_saída ), .Zero(estrutura_ula_1_zero), .\Saída_do_overflow (Overflow));
  and and_2 (and_2_out, IR_q[26], IR_q[27], IR_q[28], IR_q[29], ~IR_q[30], ~IR_q[31]);  // AND_Gate
  and and_3 (and_3_out, ~IR_q[26], ~IR_q[27], IR_q[28], ~IR_q[29], ~IR_q[30], IR_q[31]);  // AND_Gate

  // Notes on the sheet:
  //   Entrada de 32 bits do IR
  //   O IR FUNCIONA COM UMA INSTRUÇÃO
  //   Operador do clock
  //   para gravar a informação no registrador
  //   Entrada do BR
  //   Registrado e informa qual OPERADOR será usado
  //   Operador do
  //   primeiro MUX
  //   Operador do
  //   segundo MUX
  //   Esses fios será os valores da segunda entrada de B da ULA
  //   A
  //   B
  //   Operador de B
  //   Operado da ULA
  //   A segunda entrada do PC será uma escolha rápida do PC
  //   onde o IR informará qual o valor da próxima instrução mais rápido
  //   tipo: ele pode pular da memória 01 para 20 sem antes passar pelas 19 casinhas
  //   Zero
  //   Essa operação selecionará a operação do PC
  //   Pegando o valor da saída de ZERO
  //   Saída da ULA
  //   Essa operação selecionará a entrada de B da ULA
endmodule

module Processador (
  output [31:0] out_1
);

  wire button_1_out, clock_1_out, micro_processador_1_overflow;
  wire [3:0] \micro_processador_1_saída_do_pc , \micro_processador_1_saída_do_pc_2 ;
  wire [31:0] adder_1_out, ram_1_data;

  Hex_Digit_Display hex_digit_display_1 (.value(\micro_processador_1_saída_do_pc ));  // open: dp
  Hex_Digit_Display hex_digit_display_2 (.value(\micro_processador_1_saída_do_pc_2 ));  // open: dp
  Button button_1 (.out(button_1_out));
  Clock clock_1 (.out(clock_1_out));
  Micro_Processador micro_processador_1 (
    .Entrada_do_IR(out_1), .Reset(button_1_out), .Clock(clock_1_out),
    .\Saída_do_PC ({\micro_processador_1_saída_do_pc , \micro_processador_1_saída_do_pc_2 }),
    .Overflow(micro_processador_1_overflow));
  RAM #(.dataWidth(32)) ram_1 (
    .addr({\micro_processador_1_saída_do_pc , \micro_processador_1_saída_do_pc_2 }), .data(ram_1_data));  // open: sel, clk, ld, clr
  Adder #(.width(32)) adder_1 (.a(out_1), .b(ram_1_data), .out(adder_1_out));  // open: cin, cout
  LED led_1 (.in(micro_processador_1_overflow));
  Register #(.width(32)) register_1 (.D(adder_1_out), .Q(out_1), .clk(clock_1_out), .clr(button_1_out));  // open: en

  // Notes on the sheet:
  //   Clear (Reset)
  //   Clock
  //   PC
  //   Memória
  //   A memória terá as informações de dados que serão passadas pelo pulso do clock que está conectado no PC
  //   O PC é o responsável para informar a memória a próxima instrução, que serão armazenados no IR
  //   O IR é o controlador, onde informa através da entrada qual operador será executado.
  //   IR
  //   Overflow
endmodule

module Somador_BR (
  input  [31:0] in_1,
  output [31:0] out_2,
  output [31:0] out_3,
  output [31:0] out_4
);

  wire Clock_out, Reset_out;
  wire [3:0] \pc_1_saída , \pc_1_saída_2 ;
  wire [31:0] adder_1_out, ram_1_data;

  Hex_Digit_Display hex_digit_display_1 (.value(\pc_1_saída ));  // open: dp
  Hex_Digit_Display hex_digit_display_2 (.value(\pc_1_saída_2 ));  // open: dp
  Button Reset (.out(Reset_out));
  Clock Clock (.out(Clock_out));
  PC pc_1 (.\Saída ({\pc_1_saída , \pc_1_saída_2 }), .Clock(Clock_out), .Reset(Reset_out), .in_1(8'h1));
  RAM #(.dataWidth(32)) ram_1 (.addr({\pc_1_saída , \pc_1_saída_2 }), .data(ram_1_data));  // open: sel, clk, ld, clr
  Banco_Registradores banco_registradores_1 (
    .Clock(Clock_out), .\Saída_A (out_3), .\Saída_B (out_4), .Reset(Reset_out), .Entrada(in_1),
    .Op_C(out_2[4:0]), .Op_1(out_2[4:0]), .Op_2(out_2[4:0]));
  Adder #(.width(32)) adder_1 (.a(out_2), .b(ram_1_data), .out(adder_1_out));  // open: cin, cout
  Register #(.width(32)) register_1 (.D(adder_1_out), .Q(out_2), .clk(Clock_out), .clr(Reset_out));  // open: en

  // Notes on the sheet:
  //   Memória
endmodule

module Somador_BR_ULA (
  output [31:0] out_1,
  output out_2,
  output out_3
);

  wire Clock_out, Reset_out;
  wire [7:0] \pc_1_saída ;
  wire [31:0] adder_1_out, \banco_registradores_1_saída_a , \banco_registradores_1_saída_b ,
       \estrutura_ula_1_saída , ram_1_data;

  Button Reset (.out(Reset_out));
  Clock Clock (.out(Clock_out));
  PC pc_1 (.\Saída (\pc_1_saída ), .Clock(Clock_out), .Reset(Reset_out), .in_1(8'h1));
  RAM #(.dataWidth(32)) ram_1 (.addr(\pc_1_saída ), .data(ram_1_data));  // open: sel, clk, ld, clr
  Adder #(.width(32)) adder_1 (.a(out_1), .b(ram_1_data), .out(adder_1_out));  // open: cin, cout
  Register #(.width(32)) register_1 (.D(adder_1_out), .Q(out_1), .clk(Clock_out), .clr(Reset_out));  // open: en
  Banco_Registradores banco_registradores_1 (
    .Clock(Clock_out), .\Saída_A (\banco_registradores_1_saída_a ),
    .\Saída_B (\banco_registradores_1_saída_b ), .Reset(Reset_out), .Entrada(\estrutura_ula_1_saída ),
    .Op_C(out_1[15:11]), .Op_1(out_1[25:21]), .Op_2(out_1[20:16]));
  Estrutura_ULA estrutura_ula_1 (
    .Valor_A(\banco_registradores_1_saída_a ), .Valor_B(\banco_registradores_1_saída_b ),
    .in_2(out_1[31:26]), .\Saída (\estrutura_ula_1_saída ), .Zero(out_2), .\Saída_do_overflow (out_3));
endmodule
